# Fritzing sketch Arduino GPS Satellite (saved by Fritzing 0.9.7b)

parts:
  Part1 = Arduino Uno (Rev3)
  Part2 = BME280 Breakout
  U2 = D2523T [package=em406]  # not connected
  R1 = Resistor [tolerance=±5% power=0.25 resistance=10 package=THT]
  LED1 = LED - 3mm [color="Red (633nm)" current=0.030 package="3 mm [THT]"]
  R2 = Resistor [tolerance=±5% power=0.25 resistance=10k package=THT]
  U3 = SPDT Slide Switch [package=ayz0202]
  BAT1 = BC9VPC [package=bc9vpc]
  ANT1 = Antenna  # not connected
  U4 = ESP8266 WiFi Module [part_number=ESP8266]
  LED2 = LED - 3mm [color="Green (555nm)" current=0.030 package="3 mm [THT]"]

nets:
  N1: Part1.A4/SDA, Part2.SDI/SDA
  N2: Part1.A5/SCL, Part2.SCK/SCL
  GND: Part1.GND, Part2.GND, LED1.anode
  N3: Part1.D0/RX, U4.RX
  N4: Part1.D1/TX, U4.TX
  N5: Part1.D6_PWM, R2.Pin_0
  N6: Part1.D7, R1.Pin_0
  3V3: Part1.3V3, Part2.3.3V
  N7: Part1.5V, U4.3.3V#26
  N8: R2.Pin_1, LED2.cathode
  N9: U3.4, BAT1.V+
  N10: U4.GND, LED2.anode

notes:
  PA1010D
  KIM1 Satellite
  BME280
